// Logisim project Logisim AlarmClock.circ as structural Verilog: 4 circuits, main circuit Compare
module Compare (
  input  A0,
  input  B0,
  input  A1,
  input  B1,
  input  A2,
  input  B2,
  input  A3,
  input  B3,
  input  A4,
  input  B4,
  input  A5,
  input  B5,
  input  A6,
  input  B6,
  output out_15
);

  wire xnor_1_out, xnor_2_out, xnor_3_out, xnor_4_out, xnor_5_out, xnor_6_out, xnor_7_out;

  xnor xnor_1 (xnor_1_out, A1, B1);
  xnor xnor_2 (xnor_2_out, A0, B0);
  xnor xnor_3 (xnor_3_out, A2, B2);
  xnor xnor_4 (xnor_4_out, A3, B3);
  xnor xnor_5 (xnor_5_out, A4, B4);
  xnor xnor_6 (xnor_6_out, A5, B5);
  xnor xnor_7 (xnor_7_out, A6, B6);
  and and_1 (out_15, xnor_7_out, xnor_6_out, xnor_5_out, xnor_4_out, xnor_3_out, xnor_1_out, xnor_2_out);
endmodule

module Hours (
  input  ClockPulse,
  input  StackDump,
  output AMPM_LED,
  output Hour0,
  output Hour1,
  output Hour2,
  output Hour3,
  output Hour4,
  output CompareOutput
);

  wire and_1_out, and_2_out, and_3_out, and_4_out, d_ff_2_q, d_ff_4_q, d_ff_6_q, d_ff_8_q, d_ff_10_q,
       d_ff_11_q, j_k_ff_1_q, j_k_ff_2_q, j_k_ff_3_q, j_k_ff_4_q, j_k_ff_5_q, not_1_out, not_2_out,
       not_3_out, not_4_out, not_5_out, not_6_out, not_7_out, not_8_out, not_9_out, not_10_out, or_1_out,
       Reset_10_out, Reset_13_out, xor_1_out;

  not not_1 (not_1_out, j_k_ff_1_q);
  not not_2 (not_2_out, j_k_ff_5_q);
  not not_3 (not_3_out, j_k_ff_4_q);
  and and_1 (and_1_out, not_1_out, not_2_out, not_3_out, not_4_out, not_5_out);
  not not_4 (not_4_out, j_k_ff_3_q);
  not not_5 (not_5_out, j_k_ff_2_q);
  J_K_Flip_Flop j_k_ff_1 (
    .J(1'b1), .K(1'b1), .clk(or_1_out), .Q(j_k_ff_1_q), .reset(Reset_13_out));  // open: Qn, preset
  xor xor_1 (xor_1_out, ClockPulse, and_1_out);
  D_Flip_Flop d_ff_1 (.D(j_k_ff_1_q), .clk(xor_1_out), .Q(Hour0));  // open: Qn, preset, reset
  D_Flip_Flop d_ff_2 (.D(Hour0), .clk(StackDump), .Q(d_ff_2_q));  // open: Qn, preset, reset
  J_K_Flip_Flop j_k_ff_2 (.J(1'b1), .K(1'b1), .clk(xor_1_out), .Q(j_k_ff_2_q));  // open: Qn, preset, reset
  D_Flip_Flop d_ff_3 (.D(j_k_ff_2_q), .clk(xor_1_out), .Q(Hour1));  // open: Qn, preset, reset
  J_K_Flip_Flop j_k_ff_3 (
    .J(j_k_ff_2_q), .K(j_k_ff_2_q), .clk(xor_1_out), .Q(j_k_ff_3_q), .reset(or_1_out));  // open: Qn, preset
  not not_6 (not_6_out, j_k_ff_2_q);
  not not_7 (not_7_out, j_k_ff_4_q);
  not not_8 (not_8_out, j_k_ff_5_q);
  and and_2 (and_2_out, j_k_ff_1_q, not_6_out, j_k_ff_3_q, not_7_out, not_8_out);
  D_Flip_Flop d_ff_4 (.D(Hour1), .clk(StackDump), .Q(d_ff_4_q));  // open: Qn, preset, reset
  D_Flip_Flop d_ff_5 (.D(j_k_ff_3_q), .clk(xor_1_out), .Q(Hour2));  // open: Qn, preset, reset
  and and_3 (and_3_out, j_k_ff_2_q, j_k_ff_3_q);
  J_K_Flip_Flop j_k_ff_4 (
    .J(and_3_out), .K(and_3_out), .clk(xor_1_out), .Q(j_k_ff_4_q), .reset(or_1_out));  // open: Qn, preset
  D_Flip_Flop d_ff_6 (.D(Hour2), .clk(StackDump), .Q(d_ff_6_q));  // open: Qn, preset, reset
  Compare compare_1 (
    .A0(d_ff_11_q), .B0(AMPM_LED), .A1(1'b0), .B1(1'b0), .A2(d_ff_10_q), .B2(Hour4), .A3(d_ff_8_q),
    .B3(Hour3), .A4(d_ff_6_q), .B4(Hour2), .A5(d_ff_4_q), .B5(Hour1), .A6(d_ff_2_q), .B6(Hour0),
    .out_15(CompareOutput));
  D_Flip_Flop d_ff_7 (.D(j_k_ff_4_q), .clk(xor_1_out), .Q(Hour3));  // open: Qn, preset, reset
  and and_4 (and_4_out, and_3_out, j_k_ff_4_q);
  D_Flip_Flop d_ff_8 (.D(Hour3), .clk(StackDump), .Q(d_ff_8_q));  // open: Qn, preset, reset
  J_K_Flip_Flop j_k_ff_5 (
    .J(and_4_out), .K(and_4_out), .clk(xor_1_out), .Q(j_k_ff_5_q), .reset(or_1_out));  // open: Qn, preset
  or or_1 (or_1_out, Reset_10_out, Reset_13_out);
  D_Flip_Flop d_ff_9 (.D(j_k_ff_5_q), .clk(xor_1_out), .Q(Hour4));  // open: Qn, preset, reset
  and Reset_10 (Reset_10_out, j_k_ff_3_q, j_k_ff_5_q);
  D_Flip_Flop d_ff_10 (.D(Hour4), .clk(StackDump), .Q(d_ff_10_q));  // open: Qn, preset, reset
  and Reset_13 (Reset_13_out, j_k_ff_1_q, j_k_ff_2_q, j_k_ff_3_q, not_9_out, not_10_out);
  not not_9 (not_9_out, j_k_ff_4_q);
  not not_10 (not_10_out, j_k_ff_5_q);
  J_K_Flip_Flop j_k_ff_6 (.J(and_2_out), .K(and_2_out), .clk(Reset_13_out), .Q(AMPM_LED));  // open: Qn, preset, reset
  D_Flip_Flop d_ff_11 (.D(AMPM_LED), .clk(StackDump), .Q(d_ff_11_q));  // open: Qn, preset, reset
endmodule

module Minutes (
  input  ClockPulse,
  input  StackDump,
  output Increment_Hour,
  output Minute0,
  output Minute1,
  output Minute2,
  output Minute3,
  output Minute4,
  output Minute5,
  output Minute6,
  output CompareOutput
);

  wire and_1_out, and_2_out, and_3_out, and_4_out, and_5_out, d_ff_3_q, d_ff_4_q, d_ff_6_q, d_ff_7_q,
       d_ff_9_q, d_ff_11_q, d_ff_13_q, j_k_ff_1_q, j_k_ff_2_q, j_k_ff_3_q, j_k_ff_4_q, j_k_ff_5_q,
       j_k_ff_6_q, j_k_ff_7_q, not_1_out, not_2_out, not_3_out, not_4_out, not_5_out, not_6_out, not_7_out;

  J_K_Flip_Flop j_k_ff_1 (.J(1'b1), .K(1'b1), .clk(and_5_out), .Q(j_k_ff_1_q), .reset(and_2_out));  // open: Qn, preset
  J_K_Flip_Flop j_k_ff_2 (
    .J(j_k_ff_1_q), .K(j_k_ff_1_q), .clk(and_5_out), .Q(j_k_ff_2_q), .reset(and_2_out));  // open: Qn, preset
  D_Flip_Flop d_ff_1 (.D(j_k_ff_1_q), .clk(ClockPulse), .Q(Minute0));  // open: Qn, preset, reset
  and and_1 (and_1_out, j_k_ff_1_q, j_k_ff_2_q);
  D_Flip_Flop d_ff_2 (.D(j_k_ff_2_q), .clk(ClockPulse), .Q(Minute1));  // open: Qn, preset, reset
  D_Flip_Flop d_ff_3 (.D(Minute0), .clk(StackDump), .Q(d_ff_3_q));  // open: Qn, preset, reset
  J_K_Flip_Flop j_k_ff_3 (
    .J(and_1_out), .K(and_1_out), .clk(and_5_out), .Q(j_k_ff_3_q), .reset(and_2_out));  // open: Qn, preset
  D_Flip_Flop d_ff_4 (.D(Minute1), .clk(StackDump), .Q(d_ff_4_q));  // open: Qn, preset, reset
  and and_2 (and_2_out, j_k_ff_2_q, j_k_ff_3_q);
  D_Flip_Flop d_ff_5 (.D(j_k_ff_3_q), .clk(ClockPulse), .Q(Minute2));  // open: Qn, preset, reset
  D_Flip_Flop d_ff_6 (.D(Minute2), .clk(StackDump), .Q(d_ff_6_q));  // open: Qn, preset, reset
  not not_1 (not_1_out, Minute0);
  not not_2 (not_2_out, Minute1);
  not not_3 (not_3_out, Minute2);
  and AT_0 (Increment_Hour, not_1_out, not_2_out, not_3_out, not_4_out, not_5_out, not_6_out, not_7_out);
  not not_4 (not_4_out, Minute3);
  not not_5 (not_5_out, Minute4);
  not not_6 (not_6_out, Minute5);
  not not_7 (not_7_out, Minute6);
  J_K_Flip_Flop j_k_ff_4 (.J(1'b1), .K(1'b1), .clk(ClockPulse), .Q(j_k_ff_4_q), .reset(and_5_out));  // open: Qn, preset
  D_Flip_Flop d_ff_7 (.D(Minute3), .clk(StackDump), .Q(d_ff_7_q));  // open: Qn, preset, reset
  Compare compare_1 (
    .A0(d_ff_13_q), .B0(Minute6), .A1(d_ff_11_q), .B1(Minute5), .A2(d_ff_9_q), .B2(Minute4), .A3(d_ff_7_q),
    .B3(Minute3), .A4(d_ff_6_q), .B4(Minute2), .A5(d_ff_4_q), .B5(Minute1), .A6(d_ff_3_q), .B6(Minute0),
    .out_15(CompareOutput));
  J_K_Flip_Flop j_k_ff_5 (
    .J(j_k_ff_4_q), .K(j_k_ff_4_q), .clk(ClockPulse), .Q(j_k_ff_5_q), .reset(and_5_out));  // open: Qn, preset
  D_Flip_Flop d_ff_8 (.D(j_k_ff_4_q), .clk(ClockPulse), .Q(Minute3));  // open: Qn, preset, reset
  D_Flip_Flop d_ff_9 (.D(Minute4), .clk(StackDump), .Q(d_ff_9_q));  // open: Qn, preset, reset
  D_Flip_Flop d_ff_10 (.D(j_k_ff_5_q), .clk(ClockPulse), .Q(Minute4));  // open: Qn, preset, reset
  D_Flip_Flop d_ff_11 (.D(Minute5), .clk(StackDump), .Q(d_ff_11_q));  // open: Qn, preset, reset
  and and_3 (and_3_out, j_k_ff_4_q, j_k_ff_5_q);
  J_K_Flip_Flop j_k_ff_6 (
    .J(and_3_out), .K(and_3_out), .clk(ClockPulse), .Q(j_k_ff_6_q), .reset(and_5_out));  // open: Qn, preset
  D_Flip_Flop d_ff_12 (.D(j_k_ff_6_q), .clk(ClockPulse), .Q(Minute5));  // open: Qn, preset, reset
  D_Flip_Flop d_ff_13 (.D(Minute6), .clk(StackDump), .Q(d_ff_13_q));  // open: Qn, preset, reset
  and and_4 (and_4_out, and_3_out, j_k_ff_6_q);
  J_K_Flip_Flop j_k_ff_7 (
    .J(and_4_out), .K(and_4_out), .clk(ClockPulse), .Q(j_k_ff_7_q), .reset(and_5_out));  // open: Qn, preset
  D_Flip_Flop d_ff_14 (.D(j_k_ff_7_q), .clk(ClockPulse), .Q(Minute6));  // open: Qn, preset, reset
  and and_5 (and_5_out, j_k_ff_5_q, j_k_ff_7_q);

  // Notes on the sheet:
  //   Minutes Counter 0 - 9 (000 - 1001)
endmodule

module main (
  input  SetHour,
  input  h_plus,
  input  SetMinute,
  input  m_plus,
  input  SetAlarm,
  input  EnableAlarm,
  input  M_plus_2,
  input  H_plus_2
);

  wire and_1_out, and_2_out, and_3_out, and_4_out, and_5_out, and_6_out, and_7_out, and_8_out, and_9_out,
       and_10_out, and_11_out, clock_1_out, hours_1_ampm_led, hours_1_compareoutput, minutes_1_compareoutput,
       minutes_1_increment_hour, not_1_out, not_2_out, not_3_out, not_4_out, not_5_out, not_6_out, not_7_out,
       not_8_out, not_9_out, not_10_out, not_11_out, not_12_out, not_13_out, not_14_out, or_1_out, or_2_out,
       or_3_out, xor_1_out, xor_2_out, xor_3_out, xor_4_out, xor_5_out, xor_6_out;
  wire [0:0] hours_1_hour0;
  wire [2:0] minutes_1_minute0;
  wire [3:0] hours_1_hour1, minutes_1_minute3;

  not not_1 (not_1_out, SetHour);
  Clock clock_1 (.out(clock_1_out));
  not not_2 (not_2_out, H_plus_2);
  xor xor_1 (xor_1_out, H_plus_2, not_2_out);
  and and_1 (and_1_out, not_1_out, clock_1_out);
  not not_3 (not_3_out, M_plus_2);
  xor xor_2 (xor_2_out, M_plus_2, not_3_out);
  not not_4 (not_4_out, xor_1_out);
  not not_5 (not_5_out, xor_2_out);
  not not_6 (not_6_out, m_plus);
  LED AlarmTrigger (.in(and_5_out));
  not not_7 (not_7_out, h_plus);
  xor xor_3 (xor_3_out, m_plus, not_6_out);
  and and_2 (and_2_out, not_5_out, SetAlarm);
  not not_8 (not_8_out, and_2_out);
  and and_3 (and_3_out, SetAlarm, not_4_out);
  not not_9 (not_9_out, and_3_out);
  Hex_Digit_Display hex_digit_display_1 (.value({3'b000, hours_1_hour0[0]}));  // open: dp
  not not_10 (not_10_out, SetAlarm);
  not not_11 (not_11_out, SetHour);
  and and_4 (and_4_out, SetHour, xor_4_out);
  xor xor_4 (xor_4_out, h_plus, not_7_out);
  and and_5 (and_5_out, EnableAlarm, and_10_out);
  not not_12 (not_12_out, SetAlarm);
  not not_13 (not_13_out, SetMinute);
  and and_6 (and_6_out, SetMinute, xor_3_out);
  and and_7 (and_7_out, not_8_out, SetAlarm);
  not not_14 (not_14_out, and_7_out);
  and and_8 (and_8_out, SetAlarm, not_9_out);
  LED AMPM (.in(hours_1_ampm_led));
  LED led_1 (.in(hours_1_ampm_led));
  Hex_Digit_Display hex_digit_display_2 (.value(hours_1_hour1));  // open: dp
  and and_9 (and_9_out, minutes_1_increment_hour, not_10_out, not_11_out);
  or or_1 (or_1_out, and_9_out, or_2_out);
  or or_2 (or_2_out, and_4_out, and_3_out);
  and and_10 (and_10_out, hours_1_compareoutput, minutes_1_compareoutput);
  and and_11 (and_11_out, not_12_out, not_13_out, and_1_out);
  xor xor_5 (xor_5_out, and_11_out, or_3_out);
  or or_3 (or_3_out, and_6_out, and_2_out);
  xor xor_6 (xor_6_out, not_14_out, and_8_out);
  Hex_Digit_Display hex_digit_display_3 (.value({1'b0, minutes_1_minute0}));  // open: dp
  Hex_Digit_Display hex_digit_display_4 (.value(minutes_1_minute3));  // open: dp
  Hours hours_1 (
    .ClockPulse(or_1_out), .StackDump(xor_6_out), .AMPM_LED(hours_1_ampm_led), .Hour0(hours_1_hour0[0]),
    .Hour1(hours_1_hour1[0]), .Hour2(hours_1_hour1[1]), .Hour3(hours_1_hour1[2]), .Hour4(hours_1_hour1[3]),
    .CompareOutput(hours_1_compareoutput));
  Minutes minutes_1 (
    .ClockPulse(xor_5_out), .StackDump(xor_6_out), .Increment_Hour(minutes_1_increment_hour),
    .Minute0(minutes_1_minute0[0]), .Minute1(minutes_1_minute0[1]), .Minute2(minutes_1_minute0[2]),
    .Minute3(minutes_1_minute3[0]), .Minute4(minutes_1_minute3[1]), .Minute5(minutes_1_minute3[2]),
    .Minute6(minutes_1_minute3[3]), .CompareOutput(minutes_1_compareoutput));

  // Notes on the sheet:
  //   CLOCK
endmodule
